// Logisim project binaryMultiplier.circ as structural Verilog: 3 circuits, main circuit main
module main (
  input  [7:0] in_1,
  input  [7:0] in_2,
  output [15:0] out_3
);

  core_ckt core_ckt_1 (
    .A0(in_1[0]), .A1(in_1[1]), .A2(in_1[2]), .A3(in_1[3]), .A4(in_1[4]), .A5(in_1[5]), .A6(in_1[6]),
    .A7(in_1[7]), .B0(in_2[0]), .B1(in_2[1]), .B2(in_2[2]), .B3(in_2[3]), .B4(in_2[4]), .B5(in_2[5]),
    .B6(in_2[6]), .B7(in_2[7]), .op(out_3));
endmodule

module F_A (
  input  B,
  input  A,
  input  Cin,
  output Cout,
  output Sum
);

  wire and_1_out, and_2_out, xor_1_out;

  xor xor_1 (xor_1_out, A, B);
  xor xor_2 (Sum, xor_1_out, Cin);
  and and_1 (and_1_out, xor_1_out, Cin);
  and and_2 (and_2_out, B, A);
  or or_1 (Cout, and_1_out, and_2_out);
endmodule

module core_ckt (
  input  A0,
  input  A1,
  input  A2,
  input  A3,
  input  A4,
  input  A5,
  input  A6,
  input  A7,
  input  B0,
  input  B1,
  input  B2,
  input  B3,
  input  B4,
  input  B5,
  input  B6,
  input  B7,
  output [15:0] op
);

  wire and_1_out, and_2_out, and_3_out, and_4_out, and_5_out, and_6_out, and_7_out, and_8_out, and_9_out,
       and_10_out, and_11_out, and_12_out, and_13_out, and_14_out, and_15_out, and_16_out, and_17_out,
       and_18_out, and_19_out, and_20_out, and_21_out, and_22_out, and_23_out, and_24_out, and_25_out,
       and_26_out, and_27_out, and_28_out, and_29_out, and_30_out, and_31_out, and_32_out, and_33_out,
       and_34_out, and_35_out, and_36_out, and_37_out, and_38_out, and_39_out, and_40_out, and_41_out,
       and_42_out, and_43_out, and_44_out, and_45_out, and_46_out, and_47_out, and_48_out, and_49_out,
       and_50_out, and_51_out, and_52_out, and_53_out, and_54_out, and_55_out, and_56_out, and_57_out,
       and_58_out, and_59_out, and_60_out, and_61_out, and_62_out, and_63_out, f_a_2_cout, f_a_3_cout,
       f_a_3_sum, f_a_4_cout, f_a_4_sum, f_a_5_cout, f_a_5_sum, f_a_6_cout, f_a_6_sum, f_a_7_cout,
       f_a_8_cout, f_a_8_sum, f_a_9_cout, f_a_9_sum, f_a_10_cout, f_a_11_cout, f_a_11_sum, f_a_12_cout,
       f_a_12_sum, f_a_13_cout, f_a_13_sum, f_a_14_cout, f_a_14_sum, f_a_15_cout, f_a_16_cout, f_a_16_sum,
       f_a_17_cout, f_a_17_sum, f_a_18_cout, f_a_18_sum, f_a_19_cout, f_a_19_sum, f_a_20_cout, f_a_20_sum,
       f_a_21_cout, f_a_22_cout, f_a_22_sum, f_a_23_cout, f_a_23_sum, f_a_24_cout, f_a_24_sum, f_a_25_cout,
       f_a_25_sum, f_a_26_cout, f_a_26_sum, f_a_27_cout, f_a_27_sum, f_a_28_cout, f_a_29_cout, f_a_29_sum,
       f_a_30_cout, f_a_30_sum, f_a_31_cout, f_a_31_sum, f_a_32_cout, f_a_32_sum, f_a_33_cout, f_a_33_sum,
       f_a_34_cout, f_a_34_sum, f_a_35_cout, f_a_36_cout, f_a_36_sum, f_a_37_cout, f_a_37_sum, f_a_38_cout,
       f_a_38_sum, f_a_39_cout, f_a_39_sum, f_a_40_cout, f_a_40_sum, f_a_41_cout, f_a_42_cout, f_a_42_sum,
       f_a_43_cout, f_a_43_sum, f_a_44_cout, f_a_44_sum, f_a_45_cout, f_a_45_sum, f_a_46_cout, f_a_47_cout,
       f_a_47_sum, f_a_48_cout, f_a_48_sum, f_a_49_cout, f_a_49_sum, f_a_50_cout, f_a_51_cout, f_a_51_sum,
       f_a_52_cout, f_a_52_sum, f_a_53_cout, f_a_54_cout, f_a_55_cout, f_a_55_sum, f_a_56_cout, not_1_out,
       not_2_out, not_3_out, not_4_out, not_5_out;

  F_A f_a_1 (.Cin(f_a_2_cout), .Sum(op[14]), .B(f_a_3_cout), .A(and_2_out), .Cout(op[15]));
  and and_1 (and_1_out, B7, A6);
  and and_2 (and_2_out, B7, A7);
  F_A f_a_2 (.Cin(f_a_7_cout), .Sum(op[13]), .B(f_a_3_sum), .A(and_1_out), .Cout(f_a_2_cout));
  and and_3 (and_3_out, B6, A7);
  F_A f_a_3 (.Cin(f_a_6_cout), .Sum(f_a_3_sum), .B(f_a_5_cout), .A(and_3_out), .Cout(f_a_3_cout));
  and and_4 (and_4_out, B5, A7);
  F_A f_a_4 (.Cin(f_a_13_cout), .Sum(f_a_4_sum), .B(f_a_8_sum), .A(and_7_out), .Cout(f_a_4_cout));
  F_A f_a_5 (.Cin(f_a_4_cout), .Sum(f_a_5_sum), .B(f_a_8_cout), .A(and_4_out), .Cout(f_a_5_cout));
  and and_5 (and_5_out, B6, A6);
  and and_6 (and_6_out, B7, A5);
  F_A f_a_6 (.Cin(f_a_9_cout), .Sum(f_a_6_sum), .B(and_5_out), .A(f_a_5_sum), .Cout(f_a_6_cout));
  F_A f_a_7 (.Cin(f_a_10_cout), .Sum(op[12]), .B(f_a_6_sum), .A(and_6_out), .Cout(f_a_7_cout));
  and and_7 (and_7_out, B5, A6);
  and and_8 (and_8_out, B4, A7);
  F_A f_a_8 (.Cin(f_a_12_cout), .Sum(f_a_8_sum), .B(f_a_11_cout), .A(and_8_out), .Cout(f_a_8_cout));
  and and_9 (and_9_out, B6, A5);
  and and_10 (and_10_out, B7, A4);
  F_A f_a_9 (.Cin(f_a_14_cout), .Sum(f_a_9_sum), .B(and_9_out), .A(f_a_4_sum), .Cout(f_a_9_cout));
  F_A f_a_10 (.Cin(f_a_15_cout), .Sum(op[11]), .B(and_10_out), .A(f_a_9_sum), .Cout(f_a_10_cout));
  and and_11 (and_11_out, B3, A7);
  F_A f_a_11 (.Cin(f_a_17_cout), .Sum(f_a_11_sum), .B(f_a_16_cout), .A(and_11_out), .Cout(f_a_11_cout));
  and and_12 (and_12_out, B4, A6);
  and and_13 (and_13_out, B5, A5);
  F_A f_a_12 (.Cin(f_a_18_cout), .Sum(f_a_12_sum), .B(and_12_out), .A(f_a_11_sum), .Cout(f_a_12_cout));
  F_A f_a_13 (.Cin(f_a_19_cout), .Sum(f_a_13_sum), .B(f_a_12_sum), .A(and_13_out), .Cout(f_a_13_cout));
  and and_14 (and_14_out, B7, A3);
  F_A f_a_14 (.Cin(f_a_20_cout), .Sum(f_a_14_sum), .B(and_18_out), .A(f_a_13_sum), .Cout(f_a_14_cout));
  F_A f_a_15 (.Cin(f_a_21_cout), .Sum(op[10]), .B(and_14_out), .A(f_a_14_sum), .Cout(f_a_15_cout));
  and and_15 (and_15_out, B3, A6);
  and and_16 (and_16_out, B2, A7);
  F_A f_a_16 (.Cin(f_a_25_cout), .Sum(f_a_16_sum), .B(f_a_22_cout), .A(and_16_out), .Cout(f_a_16_cout));
  F_A f_a_17 (.Cin(f_a_23_cout), .Sum(f_a_17_sum), .B(f_a_16_sum), .A(and_15_out), .Cout(f_a_17_cout));
  and and_17 (and_17_out, B5, A4);
  F_A f_a_18 (.Cin(f_a_24_cout), .Sum(f_a_18_sum), .B(and_20_out), .A(f_a_17_sum), .Cout(f_a_18_cout));
  F_A f_a_19 (.Cin(f_a_26_cout), .Sum(f_a_19_sum), .B(and_17_out), .A(f_a_18_sum), .Cout(f_a_19_cout));
  and and_18 (and_18_out, B6, A4);
  F_A f_a_20 (.Cin(f_a_27_cout), .Sum(f_a_20_sum), .B(and_21_out), .A(f_a_19_sum), .Cout(f_a_20_cout));
  F_A f_a_21 (.Cin(f_a_28_cout), .Sum(op[9]), .B(and_22_out), .A(f_a_20_sum), .Cout(f_a_21_cout));
  F_A f_a_22 (.Cin(f_a_29_cout), .Sum(f_a_22_sum), .B(not_1_out), .A(and_23_out), .Cout(f_a_22_cout));
  and and_19 (and_19_out, B3, A5);
  F_A f_a_23 (.Cin(f_a_31_cout), .Sum(f_a_23_sum), .B(f_a_25_sum), .A(and_19_out), .Cout(f_a_23_cout));
  and and_20 (and_20_out, B4, A5);
  F_A f_a_24 (.Cin(f_a_32_cout), .Sum(f_a_24_sum), .B(and_25_out), .A(f_a_23_sum), .Cout(f_a_24_cout));
  and and_21 (and_21_out, B6, A3);
  and and_22 (and_22_out, B7, A2);
  not not_1 (not_1_out, 1'b1);
  and and_23 (and_23_out, A7, B1);
  and and_24 (and_24_out, B2, A6);
  F_A f_a_25 (.Cin(f_a_30_cout), .Sum(f_a_25_sum), .B(and_24_out), .A(f_a_22_sum), .Cout(f_a_25_cout));
  and and_25 (and_25_out, B4, A4);
  and and_26 (and_26_out, B5, A3);
  F_A f_a_26 (.Cin(f_a_33_cout), .Sum(f_a_26_sum), .B(and_26_out), .A(f_a_24_sum), .Cout(f_a_26_cout));
  and and_27 (and_27_out, B7, A1);
  F_A f_a_27 (.Cin(f_a_34_cout), .Sum(f_a_27_sum), .B(and_33_out), .A(f_a_26_sum), .Cout(f_a_27_cout));
  F_A f_a_28 (.Cin(f_a_35_cout), .Sum(op[8]), .B(and_27_out), .A(f_a_27_sum), .Cout(f_a_28_cout));
  and and_28 (and_28_out, B0, A7);
  and and_29 (and_29_out, A6, B1);
  F_A f_a_29 (.Cin(f_a_36_cout), .Sum(f_a_29_sum), .B(and_28_out), .A(and_29_out), .Cout(f_a_29_cout));
  and and_30 (and_30_out, B3, A4);
  and and_31 (and_31_out, B2, A5);
  F_A f_a_30 (.Cin(f_a_37_cout), .Sum(f_a_30_sum), .B(and_31_out), .A(f_a_29_sum), .Cout(f_a_30_cout));
  F_A f_a_31 (.Cin(f_a_38_cout), .Sum(f_a_31_sum), .B(f_a_30_sum), .A(and_30_out), .Cout(f_a_31_cout));
  and and_32 (and_32_out, B5, A2);
  F_A f_a_32 (.Cin(f_a_39_cout), .Sum(f_a_32_sum), .B(and_38_out), .A(f_a_31_sum), .Cout(f_a_32_cout));
  F_A f_a_33 (.Cin(f_a_40_cout), .Sum(f_a_33_sum), .B(and_32_out), .A(f_a_32_sum), .Cout(f_a_33_cout));
  and and_33 (and_33_out, B6, A2);
  and and_34 (and_34_out, B7, A0);
  F_A f_a_34 (.Cin(f_a_41_cout), .Sum(f_a_34_sum), .B(and_40_out), .A(f_a_33_sum), .Cout(f_a_34_cout));
  F_A f_a_35 (.Cin(not_2_out), .Sum(op[7]), .B(and_34_out), .A(f_a_34_sum), .Cout(f_a_35_cout));
  and and_35 (and_35_out, A5, B1);
  and and_36 (and_36_out, B0, A6);
  F_A f_a_36 (.Cin(f_a_42_cout), .Sum(f_a_36_sum), .B(and_36_out), .A(and_35_out), .Cout(f_a_36_cout));
  and and_37 (and_37_out, B3, A3);
  F_A f_a_37 (.Cin(f_a_45_cout), .Sum(f_a_37_sum), .B(and_43_out), .A(f_a_36_sum), .Cout(f_a_37_cout));
  F_A f_a_38 (.Cin(f_a_43_cout), .Sum(f_a_38_sum), .B(f_a_37_sum), .A(and_37_out), .Cout(f_a_38_cout));
  and and_38 (and_38_out, B4, A3);
  and and_39 (and_39_out, B5, A1);
  F_A f_a_39 (.Cin(f_a_44_cout), .Sum(f_a_39_sum), .B(and_44_out), .A(f_a_38_sum), .Cout(f_a_39_cout));
  F_A f_a_40 (.Cin(f_a_46_cout), .Sum(f_a_40_sum), .B(and_39_out), .A(f_a_39_sum), .Cout(f_a_40_cout));
  and and_40 (and_40_out, B6, A1);
  F_A f_a_41 (.Cin(not_2_out), .Sum(op[6]), .B(and_45_out), .A(f_a_40_sum), .Cout(f_a_41_cout));
  and and_41 (and_41_out, A4, B1);
  F_A f_a_42 (.Cin(f_a_47_cout), .Sum(f_a_42_sum), .B(and_46_out), .A(and_41_out), .Cout(f_a_42_cout));
  and and_42 (and_42_out, B3, A2);
  and and_43 (and_43_out, B2, A4);
  F_A f_a_43 (.Cin(f_a_49_cout), .Sum(f_a_43_sum), .B(f_a_45_sum), .A(and_42_out), .Cout(f_a_43_cout));
  and and_44 (and_44_out, B4, A2);
  F_A f_a_44 (.Cin(f_a_50_cout), .Sum(f_a_44_sum), .B(and_49_out), .A(f_a_43_sum), .Cout(f_a_44_cout));
  not not_2 (not_2_out, 1'b1);
  and and_45 (and_45_out, B6, A0);
  and and_46 (and_46_out, B0, A5);
  and and_47 (and_47_out, B2, A3);
  F_A f_a_45 (.Cin(f_a_48_cout), .Sum(f_a_45_sum), .B(and_47_out), .A(f_a_42_sum), .Cout(f_a_45_cout));
  and and_48 (and_48_out, B5, A0);
  and and_49 (and_49_out, B4, A1);
  F_A f_a_46 (.Cin(not_3_out), .Sum(op[5]), .B(and_48_out), .A(f_a_44_sum), .Cout(f_a_46_cout));
  and and_50 (and_50_out, B0, A4);
  and and_51 (and_51_out, A3, B1);
  F_A f_a_47 (.Cin(f_a_51_cout), .Sum(f_a_47_sum), .B(and_50_out), .A(and_51_out), .Cout(f_a_47_cout));
  and and_52 (and_52_out, B2, A2);
  and and_53 (and_53_out, B3, A1);
  F_A f_a_48 (.Cin(f_a_52_cout), .Sum(f_a_48_sum), .B(and_52_out), .A(f_a_47_sum), .Cout(f_a_48_cout));
  F_A f_a_49 (.Cin(f_a_53_cout), .Sum(f_a_49_sum), .B(f_a_48_sum), .A(and_53_out), .Cout(f_a_49_cout));
  and and_54 (and_54_out, B4, A0);
  F_A f_a_50 (.Cin(not_3_out), .Sum(op[4]), .B(and_54_out), .A(f_a_49_sum), .Cout(f_a_50_cout));
  and and_55 (and_55_out, A2, B1);
  F_A f_a_51 (.Cin(f_a_55_cout), .Sum(f_a_51_sum), .B(and_57_out), .A(and_55_out), .Cout(f_a_51_cout));
  and and_56 (and_56_out, B3, A0);
  F_A f_a_52 (.Cin(f_a_54_cout), .Sum(f_a_52_sum), .B(and_59_out), .A(f_a_51_sum), .Cout(f_a_52_cout));
  F_A f_a_53 (.Cin(not_4_out), .Sum(op[3]), .B(f_a_52_sum), .A(and_56_out), .Cout(f_a_53_cout));
  not not_3 (not_3_out, 1'b1);
  and and_57 (and_57_out, B0, A3);
  and and_58 (and_58_out, A1, B1);
  and and_59 (and_59_out, B2, A1);
  F_A f_a_54 (.Cin(not_4_out), .Sum(op[2]), .B(and_61_out), .A(f_a_55_sum), .Cout(f_a_54_cout));
  and and_60 (and_60_out, B0, A2);
  F_A f_a_55 (.Cin(f_a_56_cout), .Sum(f_a_55_sum), .B(and_60_out), .A(and_58_out), .Cout(f_a_55_cout));
  not not_4 (not_4_out, 1'b1);
  and and_61 (and_61_out, B2, A0);
  and and_62 (and_62_out, B0, A1);
  and and_63 (and_63_out, B1, A0);
  F_A f_a_56 (.Cin(not_5_out), .Sum(op[1]), .B(and_62_out), .A(and_63_out), .Cout(f_a_56_cout));
  not not_5 (not_5_out, 1'b1);
  and and_64 (op[0], B0, A0);
endmodule
